# Fritzing sketch Luces (saved by Fritzing 0.9.1b)
breadboards: 1

parts:
  S1 = Pushbutton [package="[THT]"]
  R1 = Resistor [tolerance=±5% resistance=10k package=THT]
  R2 = Resistor [tolerance=±5% resistance=10k package=THT]
  Parte1 = Arduino Uno (Rev3)
  S2 = Pushbutton [package="[THT]"]

nets:
  N1: S1.Pin_1, S1.Pin_2, R1.Pin_0, Parte1.D9_PWM
  N2: S1.Pin_3, S1.Pin_4, Parte1.5V, S2.Pin_1, S2.Pin_2
  N3: R1.Pin_1, R2.Pin_0, Parte1.GND
  N4: R2.Pin_1, Parte1.D8, S2.Pin_3, S2.Pin_4

notes:
  El circuito que se muestra es entre un botón y un timbre (también botón).
  La conexión para un switch es similar. Hay que conectar la corriente donde el contacto es constante. Lo demas cambia sólo en el código.

// code stored in the sketch: Luces-fzz.ino
/*
Esta aplicación tiene como objetivo probar la interacción entre dos 
elementos que cambian el estado de la misma luz. 
En este caso, buttonPin representa un botón y ringPin un timbre o switch.
En el caso real, en lugar del botón, la interacción se dará mediante un servicio web
por medio de wifi.
*/


int ledPin = 7;
int buttonPin = 9;
int ringPin = 8;

boolean reading;
boolean flag = false;
boolean switchStatus = false;


void setup(){
  pinMode(ledPin, OUTPUT);
  pinMode(buttonPin, INPUT);  
  pinMode(ringPin, INPUT);
  Serial.begin(9600);
  switchStatus = digitalRead(ringPin);
}

void loop(){
  changeStatus(buttonPin);
  //changeStatus(ringPin); Se elige si está conectado un timbre
  changeStatusSwitch(ringPin); // Se elige si está conectado un Switch
  digitalWrite(ledPin, flag);
}
// Para botones (timbres)
void changeStatus(int pin){
  reading = digitalRead(pin);
  if(reading){
    flag = !flag;
    while(reading){
      reading = digitalRead(pin);
    }
    delay(500);
  }  
}

// Para switches
void changeStatusSwitch(int pin){
  if(digitalRead(pin) != switchStatus){
    flag = !flag;
    switchStatus = digitalRead(pin);
    delay(500);  
  }  
}

// code stored in the sketch: Luces.ino
/*
Esta aplicación tiene como objetivo probar la interacción entre dos 
elementos que cambian el estado de la misma luz. 
En este caso, buttonPin representa un botón y ringPin un timbre o switch.
En el caso real, en lugar del botón, la interacción se dará mediante un servicio web
por medio de wifi.
*/


int ledPin = 7;
int buttonPin = 9;
int ringPin = 8;

boolean reading;
boolean flag = false;
boolean switchStatus = false;


void setup(){
  pinMode(ledPin, OUTPUT);
  pinMode(buttonPin, INPUT);  
  pinMode(ringPin, INPUT);
  Serial.begin(9600);
  switchStatus = digitalRead(ringPin);
}

void loop(){
  changeStatus(buttonPin);
  //changeStatus(ringPin); Se elige si está conectado un timbre
  changeStatusSwitch(ringPin); // Se elige si está conectado un Switch
  digitalWrite(ledPin, flag);
}
// Para botones (timbres)
void changeStatus(int pin){
  reading = digitalRead(pin);
  if(reading){
    flag = !flag;
    while(reading){
      reading = digitalRead(pin);
    }
    delay(500);
  }  
}

// Para switches
void changeStatusSwitch(int pin){
  if(digitalRead(pin) != switchStatus){
    flag = !flag;
    switchStatus = digitalRead(pin);
    delay(500);  
  }  
}
